# Fritzing sketch Circuit (saved by Fritzing 0.9.4)
breadboards: 1

parts:
  BeagleBone1 = BeagleBone Black
  LED1 = LED - 3mm [color="Red (633nm)" package="3 mm [THT]"]
  R1 = Resistor [tolerance=±5% resistance=1k package=THT]
  S2 = Tactile Switch Buttons - 12mm Square [package=tactile-pth-12mm]
  R3 = Resistor [tolerance=±5% resistance=10k package=THT]

nets:
  N1: BeagleBone1.no_name_yet#2, R1.Pin_1, R3.Pin_0
  N2: BeagleBone1.no_name_yet#4, S2.2, S2.4
  N3: BeagleBone1.no_name_yet#108, S2.1, S2.3, R3.Pin_1
  N4: BeagleBone1.no_name_yet#112, LED1.anode
  N5: LED1.cathode, R1.Pin_0

custom parts:
  BeagleBone Black: BeagleBone Black rev. A5B
  Tactile Switch Buttons - 12mm Square: Medium-sized clicky momentary switches are standard input "buttons" on electronic projects. These work best in a PCB but can be used on a solderless breadboard as shown in this tutorial. The pins are normally open (disconnected) and when the button is pressed they are momentarily closed. They come in a pack of 10, they're pretty handy so you'll want to keep them around. You can find an EAGLE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
