# Fritzing sketch Circuit (saved by Fritzing 0.9.4)
breadboards: 1

parts:
  BeagleBone1 = BeagleBone Black
  LED1 = LED - 3mm [color="Red (633nm)" package="3 mm [THT]"]
  R1 = Resistor [tolerance=±5% resistance=1k package=THT]

nets:
  N1: BeagleBone1.no_name_yet#2, R1.Pin_1
  N2: BeagleBone1.no_name_yet#112, LED1.anode
  N3: LED1.cathode, R1.Pin_0

custom parts:
  BeagleBone Black: BeagleBone Black rev. A5B
