# Fritzing sketch Circuit (saved by Fritzing 0.9.4)
breadboards: 1

parts:
  BeagleBone1 = BeagleBone Black
  LED1 = LED - 3mm [color="Red (633nm)" package="3 mm [THT]"]
  R1 = Resistor [tolerance=±5% resistance=1k package=THT]
  R2 = Resistor [tolerance=±5% resistance=1k package=THT]
  LED2 = LED - 3mm [color="Yellow (585nm)" package="3 mm [THT]"]

nets:
  N1: BeagleBone1.no_name_yet#2, R1.Pin_1, R2.Pin_1
  N2: BeagleBone1.no_name_yet#112, LED1.anode
  N3: BeagleBone1.no_name_yet#114, LED2.anode
  N4: LED1.cathode, R1.Pin_0
  N5: R2.Pin_0, LED2.cathode

custom parts:
  BeagleBone Black: BeagleBone Black rev. A5B
