# Fritzing sketch Circuit (saved by Fritzing 0.9.4)
breadboards: 1

parts:
  BeagleBone1 = BeagleBone Black
  S2 = Tactile Switch Buttons - 12mm Square [package=tactile-pth-12mm]
  R3 = Resistor [tolerance=±5% resistance=10k package=THT]
  S3 = Tactile Switch Buttons - 12mm Square [package=tactile-pth-12mm]
  R4 = Resistor [tolerance=±5% resistance=10k package=THT]
  LED1 = LED - 3mm [color="White (6500K)" package="3 mm [THT]"]
  LED2 = LED - 3mm [color="Blue (430nm)" package="3 mm [THT]"]
  LED3 = LED - 3mm [color="Green (555nm)" package="3 mm [THT]"]
  LED4 = LED - 3mm [color="Yellow (585nm)" package="3 mm [THT]"]
  LED5 = LED - 3mm [color="Red (633nm)" package="3 mm [THT]"]
  R5 = Resistor [tolerance=±5% resistance=1k package=THT]
  R6 = Resistor [tolerance=±5% resistance=1k package=THT]
  R7 = Resistor [tolerance=±5% resistance=1k package=THT]
  R8 = Resistor [tolerance=±5% resistance=1k package=THT]
  R9 = Resistor [tolerance=±5% resistance=1k package=THT]

nets:
  N1: BeagleBone1.no_name_yet#2, R3.Pin_0, R4.Pin_0, R5.Pin_0, R6.Pin_0, R7.Pin_0, R8.Pin_0, R9.Pin_0
  N2: BeagleBone1.no_name_yet#4, S2.2, S2.4, S3.2, S3.4
  N3: BeagleBone1.no_name_yet#108, S2.1, S2.3, R3.Pin_1
  N4: BeagleBone1.no_name_yet#110, S3.1, S3.3, R4.Pin_1
  N5: BeagleBone1.no_name_yet#112, LED5.anode
  N6: BeagleBone1.no_name_yet#114, LED4.cathode, R7.Pin_1
  N7: BeagleBone1.no_name_yet#116, LED3.anode
  N8: BeagleBone1.no_name_yet#118, LED2.anode
  N9: BeagleBone1.no_name_yet#126, LED1.anode
  N10: LED1.cathode, R5.Pin_1
  N11: LED2.cathode, R9.Pin_1
  N12: LED3.cathode, R8.Pin_1
  N13: LED5.cathode, R6.Pin_1

custom parts:
  BeagleBone Black: BeagleBone Black rev. A5B
  Tactile Switch Buttons - 12mm Square: Medium-sized clicky momentary switches are standard input "buttons" on electronic projects. These work best in a PCB but can be used on a solderless breadboard as shown in this tutorial. The pins are normally open (disconnected) and when the button is pressed they are momentarily closed. They come in a pack of 10, they're pretty handy so you'll want to keep them around. You can find an EAGLE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
