# Fritzing sketch Circuit (saved by Fritzing 0.9.4)
breadboards: 1

parts:
  BeagleBone1 = BeagleBone Black
  R1 = Resistor [tolerance=±5% resistance=1k package=THT]
  LED2 = LED - 3mm [color="White (6500K)" package="3 mm [THT]"]

nets:
  N1: BeagleBone1.no_name_yet#2, R1.Pin_1
  N2: BeagleBone1.no_name_yet#119, LED2.anode
  N3: R1.Pin_0, LED2.cathode

custom parts:
  BeagleBone Black: BeagleBone Black rev. A5B
