# Fritzing sketch Circuit (saved by Fritzing 0.9.4)
breadboards: 1

parts:
  BeagleBone1 = BeagleBone Black
  R1 = Resistor [tolerance=±5% resistance=1k package=THT]
  LED2 = LED - 3mm [color="Blue (430nm)" package="3 mm [THT]"]
  LED3 = LED - 3mm [color="Blue (430nm)" package="3 mm [THT]"]
  LED4 = LED - 3mm [color="Red (633nm)" package="3 mm [THT]"]
  R2 = Resistor [tolerance=±5% resistance=1k package=THT]
  R3 = Resistor [tolerance=±5% resistance=1k package=THT]
  LED5 = LED - 3mm [color="Yellow (585nm)" package="3 mm [THT]"]
  LED6 = LED - 3mm [color="Green (555nm)" package="3 mm [THT]"]
  LED7 = LED - 3mm [color="White (6500K)" package="3 mm [THT]"]
  R4 = Resistor [tolerance=±5% resistance=1k package=THT]
  R5 = Resistor [tolerance=±5% resistance=1k package=THT]
  R6 = Resistor [tolerance=±5% resistance=1k package=THT]

nets:
  N1: BeagleBone1.no_name_yet#2, R1.Pin_1, R2.Pin_1, R3.Pin_1, R4.Pin_1, R5.Pin_1, R6.Pin_1
  N2: BeagleBone1.no_name_yet#22, LED3.anode
  N3: BeagleBone1.no_name_yet#112, LED4.anode
  N4: BeagleBone1.no_name_yet#114, LED5.anode
  N5: BeagleBone1.no_name_yet#116, LED6.anode
  N6: BeagleBone1.no_name_yet#118, LED7.anode
  N7: BeagleBone1.no_name_yet#126, LED2.anode
  N8: R1.Pin_0, LED2.cathode
  N9: LED3.cathode, R2.Pin_0
  N10: LED4.cathode, R3.Pin_0
  N11: LED5.cathode, R5.Pin_0
  N12: LED6.cathode, R6.Pin_0
  N13: LED7.cathode, R4.Pin_0

custom parts:
  BeagleBone Black: BeagleBone Black rev. A5B
