# Fritzing sketch Circuit (saved by Fritzing 0.9.4)
breadboards: 1

parts:
  BeagleBone1 = BeagleBone Black
  R1 = Rotary Potentiometer (Small) [maximum_resistance=100kΩ package=THT]
  R2 = Resistor [tolerance=±5% resistance=1k package=THT]
  LED1 = LED - 3mm [color="Blue (430nm)" package="3 mm [THT]"]

nets:
  N1: BeagleBone1.no_name_yet#1, R2.Pin_0
  N2: BeagleBone1.no_name_yet#32, R1.leg1
  N3: BeagleBone1.no_name_yet#34, R1.leg2
  N4: BeagleBone1.no_name_yet#39, R1.wiper
  N5: BeagleBone1.no_name_yet#113, LED1.anode
  N6: R2.Pin_1, LED1.cathode

custom parts:
  BeagleBone Black: BeagleBone Black rev. A5B
